// Digital circuit vec_adder.dig as structural Verilog
module vec_adder (
  input  [31:0] A_i,
  input  [31:0] B_i,
  input  mode_i,
  input  [1:0] vecSize_i,
  output [31:0] S_o
);

  vec_adder #(.applicationType("GHDL"), .CodeFile("/home/luiz-cavalini/AC-AVX-Adder/src/vec_adder_full.vhd")) u_vec_adder (
    .A_i(A_i), .B_i(B_i), .mode_i(mode_i), .vecSize_i(vecSize_i), .S_o(S_o));
endmodule
